# Fritzing sketch moduloesclavo (saved by Fritzing 0.9.3b)

parts:
  Componente1 = Arduino Leonardo (Rev3b)
  Componente2 = Bluetooth HC-05 Macho

nets:
  5V: Componente1.5V, Componente2.VCC
  GND: Componente1.GND, Componente2.GND
  N1: Componente1.D10_PWM/A10, Componente2.TXD
  N2: Componente1.D11_PWM, Componente2.RXD
