# Fritzing sketch modulomaestro (saved by Fritzing 0.9.3b)
breadboards: 1

parts:
  Componente1 = Arduino Nano (Rev3.0) (ICSP)
  GY1 = MPU-6050 Board GY-521 [form="♀ (female)" package=THT]
  Componente2 = Bluetooth HC-05 Macho
  S1 = Momentary Switch [package=ksa_sealed_tac_switch]
  S2 = Momentary Switch [package=ksa_sealed_tac_switch]
  S3 = Momentary Switch [package=ksa_sealed_tac_switch]

nets:
  GND: Componente1.GND, GY1.pin2, GY1.pin7, Componente2.GND, S1.2, S2.1, S2.2, S3.1, S3.2
  N1: Componente1.D2, GY1.pin8
  N2: Componente1.D3, S1.4
  N3: Componente1.D4, S2.3, S2.4
  N4: Componente1.D5, S3.3, S3.4
  N5: Componente1.D10, Componente2.TXD
  N6: Componente1.D11/MOSI, Componente2.RXD
  5V: Componente1.5V, GY1.pin1, Componente2.VCC
  N7: Componente1.A5, GY1.pin3
  N8: Componente1.A4, GY1.pin4

custom parts:
  MPU-6050 Board GY-521: Acelerometro y Giroscopio MPU-6050 Board GY-521
